# Fritzing sketch Input - pot (saved by Fritzing 0.8.5b)
breadboards: 1

parts:
  R2 = Resistor [tolerance=±5% resistance=1k package="0805 [SMD]"]
  U1 = POT [package=pot_alpha_rv16af-20]

nets:
  N1: R2.Pin_1, U1.A
