# Fritzing sketch Output - soundModule (saved by Fritzing 0.8.5b)
breadboards: 1

parts:
  Part2 = Arduino Uno (Rev3)
  C1 = Capacitor [package=cap-pth-small-kit]
  R3 = Resistor [tolerance=±5% resistance=220 package="0603 [SMD]"]
  TRRS1 = Audio Jack (TRRS) 3.5mm [part_number="LUMBERG JEITA RC-5325A" package="RC-5325A [SMD]"]

nets:
  N1: Part2.A0, C1.1, R3.Pin_1
  N2: Part2.D9_PWM, TRRS1.TIP
  N3: Part2.GND, C1.2, TRRS1.SLEEVE
